# Fritzing sketch rgb-led (saved by Fritzing 0.9.0b)
circuit board: 7cm x 5cm
breadboards: 1

parts:
  Red = Rotary Potentiometer (Large) [package=THT]
  Green = Rotary Potentiometer (Large) [package=THT]
  Blue = Rotary Potentiometer (Large) [package=THT]
  V1 = DC Power [voltage=12V]
  QR = N-Channel MOSFET [package=to220v]
  QG = N-Channel MOSFET [package=to220v]
  QB = N-Channel MOSFET [package=to220v]
  Arduino_Nano_V3_0 = Arduino Nano (Rev3.0)
  G_R_B = RGB LED Strip (common anode)

nets:
  N1: Red.leg1, Green.leg1, Blue.leg1, Arduino_Nano_V3_0.5V
  N2: Red.wiper, Arduino_Nano_V3_0.A2
  N3: Red.leg2, Green.leg2, Blue.leg2, V1.V-, QR.D, QG.D, QB.D, Arduino_Nano_V3_0.GND
  N4: Green.wiper, Arduino_Nano_V3_0.A1
  N5: Blue.wiper, Arduino_Nano_V3_0.A0
  VIN: V1.V+, Arduino_Nano_V3_0.VIN, G_R_B.VCC
  N6: QR.G, Arduino_Nano_V3_0.D3
  N7: QR.S, G_R_B.R
  N8: QG.G, Arduino_Nano_V3_0.D5
  N9: QG.S, G_R_B.G
  N10: QB.G, Arduino_Nano_V3_0.D6
  N11: QB.S, G_R_B.B

notes:
  Schema v2.2
  Breadboard Design v2.2
  DC 12V
  GND
  GND   12V
  RGB LED V2 2014
  coredump

custom parts:
  Rotary Potentiometer (Large): A rotary adjustable resistor (potentiometer).
  N-Channel MOSFET: N-Channel MOSFET, 12V, 1.5A
  RGB LED Strip (common anode): A connector for a RGB LED strip
